# Fritzing sketch ESP8266BreadboardTester (saved by Fritzing 0.9.3b)
circuit board: 3.48507cm x 2.4848cm
breadboards: 1

parts:
  ESP = ESP8266 WiFi Module [part_number=ESP8266]
  U2 = V_REG_LD1117VXX [package=78xxl]
  APA102 = Header 4 [package=molex-1x4_lock]
  C4 = Electrolytic Capacitor [capacitance=10µF package="100 mil [THT, electrolytic]"]
  1000uF = Electrolytic Capacitor [capacitance=1mF package="100 mil [THT, electrolytic]"]
  R3 = Resistor [tolerance=±5% resistance=1k package=THT]
  R2 = Resistor [tolerance=±5% resistance=1k package=THT]
  R1 = Resistor [tolerance=±5% resistance=220 package=THT]
  104 = Ceramic Capacitor [capacitance=0.1µF package="100 mil [THT, multilayer]"]
  +_- = female pin header, 2 pins [form="♀ (female)"]
  jack_switch = Header 3 [package=screwterminal-3.5mm-3_lock.007s]

nets:
  N1: ESP.VCC, U2.OUT, C4.+, R3.Pin_1, R2.Pin_1
  N2: ESP.GPIO_0, APA102.3
  N3: ESP.RST, R3.Pin_0
  N4: ESP.GPIO_2, R1.Pin_0
  N5: ESP.CH_PD, R2.Pin_0
  GND: ESP.GND, U2.GND, APA102.1, C4.-, 1000uF.-, 104.0, +_-.pin1, jack_switch.1
  N6: U2.IN, APA102.4, 1000uF.+, 104.1, jack_switch.3
  N7: APA102.2, R1.Pin_1
  N8: +_-.pin2, jack_switch.2

notes:
  Smart

custom parts:
  ESP8266 WiFi Module: Generic WiFi Module based on the ESP8266 with onboard PCB antenna and UART communications
